// Digital circuit core.dig as structural Verilog
module core (
  input  clk
);

  wire alu_op, write;
  wire [31:0] insts_memory_1_out, pc_1_out, sum_s;

  PC pc_1 (.in(sum_s), .clk(clk), .out(pc_1_out));
  Add #(.Bits(32)) sum (.a(pc_1_out), .b(32'h4), .c_i(1'b0), .s(sum_s));  // open: c_o
  Insts_Memory insts_memory_1 (.pc(pc_1_out), .out(insts_memory_1_out));
  control_unit control_unit_1 (.instr(insts_memory_1_out));
  register_unity register_unity_1 (.instr(insts_memory_1_out), .write(write));
  // ALU alu_1: pin names not known; wires that end beside it: alu_op
endmodule
